// Logisim project syncCounter.circ as structural Verilog: 1 circuit, main circuit main
module main (
  input  E
);

  wire clock_1_out, decoder_1_out0, decoder_1_out1, decoder_1_out2, decoder_1_out3, decoder_1_out4,
       decoder_1_out5, decoder_1_out6, decoder_1_out7, not_1_out, or_1_out, or_2_out, or_3_out, or_4_out,
       or_5_out, or_6_out, or_7_out, or_8_out, xor_1_out, xor_2_out;
  wire [2:0] d_ff_1_q;

  Decoder #(.select(3), .enable("false")) decoder_1 (
    .out0(decoder_1_out0), .out1(decoder_1_out1), .out2(decoder_1_out2), .out3(decoder_1_out3),
    .out4(decoder_1_out4), .out5(decoder_1_out5), .out6(decoder_1_out6), .out7(decoder_1_out7), .sel(d_ff_1_q));
  or or_1 (or_1_out, d_ff_1_q[0], d_ff_1_q[1]);
  or or_2 (or_2_out, decoder_1_out0, decoder_1_out2, decoder_1_out3, decoder_1_out5, decoder_1_out6, decoder_1_out7);
  or or_3 (or_3_out, decoder_1_out0, decoder_1_out1, decoder_1_out3, decoder_1_out4, decoder_1_out5, decoder_1_out6, decoder_1_out7);
  not not_1 (not_1_out, d_ff_1_q[0]);
  xor xor_1 (xor_1_out, d_ff_1_q[0], d_ff_1_q[1]);
  xor xor_2 (xor_2_out, or_1_out, d_ff_1_q[2]);
  Clock clock_1 (.out(clock_1_out));
  or or_4 (or_4_out, decoder_1_out0, decoder_1_out1, decoder_1_out2, decoder_1_out3, decoder_1_out4, decoder_1_out7);
  or or_5 (or_5_out, decoder_1_out0, decoder_1_out2, decoder_1_out3, decoder_1_out5, decoder_1_out6);
  D_Flip_Flop d_ff_1 (.clk(clock_1_out), .D(not_1_out), .Q(d_ff_1_q[0]), .en(E));  // open: Qn, preset, reset
  D_Flip_Flop d_ff_2 (.clk(clock_1_out), .D(xor_1_out), .Q(d_ff_1_q[1]), .en(E));  // open: Qn, preset, reset
  D_Flip_Flop d_ff_3 (.clk(clock_1_out), .D(xor_2_out), .Q(d_ff_1_q[2]), .en(E));  // open: Qn, preset, reset
  or or_6 (or_6_out, decoder_1_out0, decoder_1_out4, decoder_1_out5, decoder_1_out6);
  or or_7 (or_7_out, decoder_1_out0, decoder_1_out2, decoder_1_out6);
  or or_8 (or_8_out, decoder_1_out2, decoder_1_out3, decoder_1_out4, decoder_1_out5, decoder_1_out6);
  _7_Segment_Display u_7_segment_display_1 (
    .g(or_8_out), .f(or_6_out), .a(or_2_out), .b(or_4_out), .e(or_7_out), .d(or_5_out), .c(or_3_out));  // open: dp

  // Notes on the sheet:
  //   Clock
  //   C
  //   B
  //   A
  //   O-0
  //   O-1
  //   O-2
endmodule
