// Logisim project Half_Adder.circ as structural Verilog: 1 circuit, main circuit main
module main (
  input  Input_1__A,
  input  Input_2__B,
  input  Input_1__A_2,
  input  Input_2__B_2,
  output C,
  output S,
  output C_2,
  output S_2
);

  wire and_2_out, and_3_out, not_1_out, not_2_out;

  and and_1 (C, Input_1__A, Input_2__B);
  or or_1 (S, and_3_out, and_2_out);
  and and_2 (and_2_out, Input_1__A, not_1_out);
  and and_3 (and_3_out, not_2_out, Input_2__B);
  not not_1 (not_1_out, Input_2__B);
  not not_2 (not_2_out, Input_1__A);
  and and_4 (C_2, Input_1__A_2, Input_2__B_2);
  xor xor_1 (S_2, Input_1__A_2, Input_2__B_2);

  // Notes on the sheet:
  //   Without an XOR gate,
  //   like we will be doing
  //   on the breadboard
  //   With an XOR gate
endmodule
