// Logisim project Full_Adder.circ as structural Verilog: 1 circuit, main circuit main
module main (
  input  in_1,
  input  in_2,
  input  in_3,
  input  Input_1__X,
  input  Input_2__Y,
  input  Input_3__Z,
  input  Input_1__X_2,
  input  Input_2__Y_2,
  input  Input_3__Z_2,
  output out_10,
  output out_11,
  output C,
  output S,
  output C_2,
  output S_2
);

  wire and_1_out, and_2_out, and_3_out, and_4_out, and_5_out, xor_1_out;

  and and_1 (and_1_out, Input_1__X_2, Input_2__Y_2);
  or or_1 (C_2, and_1_out, and_2_out);
  and and_2 (and_2_out, xor_1_out, Input_3__Z_2);
  xor xor_1 (xor_1_out, Input_1__X_2, Input_2__Y_2);
  xor xor_2 (S_2, xor_1_out, Input_3__Z_2);
  Adder #(.width(1)) adder_1 (.a(in_1), .b(in_2));  // open: out, cin, cout
  Adder #(.width(1)) adder_2 (.b(in_3), .out(out_10), .cout(out_11));  // open: a, cin
  or or_2 (C, and_5_out, and_4_out, and_3_out);
  and and_3 (and_3_out, Input_2__Y, Input_3__Z);
  and and_4 (and_4_out, Input_1__X, Input_3__Z);
  and and_5 (and_5_out, Input_1__X, Input_2__Y);
  xor xor_3 (S, Input_1__X, Input_2__Y, Input_3__Z);
endmodule
