// Logisim project Decoder.circ as structural Verilog: 1 circuit, main circuit main
module main (
  input  E,
  input  E_2,
  input  I_0,
  input  I_0_2,
  input  I_1,
  input  I_1_2,
  input  E_3,
  input  I_0_3,
  input  I_1_3,
  output D_0,
  output D_0_2,
  output D_1,
  output D_1_2,
  output D_2,
  output D_2_2,
  output D_3,
  output D_3_2,
  output D_0_3,
  output D_1_3,
  output D_2_3,
  output D_3_3
);

  wire and_1_out, and_2_out, and_3_out, and_4_out, nand_1_out, nand_2_out, nand_3_out, nand_4_out,
       nand_5_out, nand_6_out, nand_7_out, nand_8_out, not_1_out, not_2_out, not_3_out, not_4_out, not_5_out,
       not_6_out, not_7_out, not_8_out, not_9_out, not_10_out, not_11_out, not_16_out, not_17_out;

  not not_1 (not_1_out, I_0_2);
  nand nand_1 (nand_1_out, not_1_out, not_2_out);
  not not_2 (not_2_out, I_1_2);
  not not_3 (not_3_out, I_0_2);
  nand nand_2 (nand_2_out, not_3_out, I_1_2);
  nand nand_3 (nand_3_out, I_0_2, not_4_out);
  not not_4 (not_4_out, I_1_2);
  nand nand_4 (nand_4_out, I_0_2, I_1_2);
  not not_5 (not_5_out, E_3);
  not not_6 (not_6_out, I_0_3);
  not not_7 (not_7_out, I_1_3);
  nand nand_5 (nand_5_out, E_2, not_8_out);
  not not_8 (not_8_out, nand_1_out);
  nand nand_6 (nand_6_out, E_2, not_9_out);
  not not_9 (not_9_out, nand_2_out);
  nand nand_7 (nand_7_out, E_2, not_10_out);
  not not_10 (not_10_out, nand_3_out);
  nand nand_8 (nand_8_out, E_2, not_11_out);
  not not_11 (not_11_out, nand_4_out);
  not not_12 (D_0_2, nand_5_out);
  not not_13 (D_1_2, nand_6_out);
  not not_14 (D_2_2, nand_7_out);
  not not_15 (D_3_2, nand_8_out);
  nand nand_9 (D_0_3, not_5_out, not_6_out, not_7_out);
  nand nand_10 (D_1_3, not_5_out, not_6_out, I_1_3);
  nand nand_11 (D_2_3, not_5_out, I_0_3, not_7_out);
  nand nand_12 (D_3_3, not_5_out, I_0_3, I_1_3);
  not not_16 (not_16_out, I_0);
  not not_17 (not_17_out, I_1);
  and and_1 (and_1_out, not_16_out, not_17_out);
  and and_2 (and_2_out, not_16_out, I_1);
  and and_3 (and_3_out, I_0, not_17_out);
  and and_4 (and_4_out, I_0, I_1);
  and and_5 (D_0, E, and_1_out);
  and and_6 (D_1, E, and_2_out);
  and and_7 (D_2, E, and_3_out);
  and and_8 (D_3, E, and_4_out);

  // Notes on the sheet:
  //   (Active High)
  //   (Active Low)
  //   (Active High)
endmodule
