// Logisim project mux.circ as structural Verilog: 1 circuit, main circuit main
module main (
  input  I_0,
  input  D,
  input  I_1,
  input  I_2,
  input  I_3,
  input  _1,
  input  I_4,
  input  _0,
  input  I_5,
  input  I_6,
  input  I_7,
  input  A,
  input  B,
  input  C,
  input  S_0,
  input  S_1,
  input  S_2,
  output Output,
  output Output_2
);

  wire and_1_out, and_2_out, and_3_out, and_4_out, and_5_out, and_6_out, and_7_out, and_8_out, and_9_out,
       and_10_out, and_11_out, and_12_out, and_13_out, and_14_out, and_15_out, and_16_out, not_1_out,
       not_2_out, not_3_out, not_4_out, not_5_out, not_6_out, not_7_out;

  not not_1 (not_1_out, S_0);
  not not_2 (not_2_out, S_1);
  not not_3 (not_3_out, S_2);
  and and_1 (and_1_out, I_0, not_1_out, not_2_out, not_3_out);
  and and_2 (and_2_out, I_1, not_1_out, not_2_out, S_2);
  and and_3 (and_3_out, I_2, not_1_out, S_1, not_3_out);
  and and_4 (and_4_out, I_3, not_1_out, S_1, S_2);
  and and_5 (and_5_out, I_4, S_0, not_2_out, not_3_out);
  and and_6 (and_6_out, I_5, S_0, not_2_out, S_2);
  and and_7 (and_7_out, I_6, S_0, S_1, not_3_out);
  and and_8 (and_8_out, I_7, S_0, S_1, S_2);
  or or_1 (Output_2, and_1_out, and_2_out, and_3_out, and_4_out, and_5_out, and_6_out, and_7_out, and_8_out);
  not not_4 (not_4_out, D);
  not not_5 (not_5_out, A);
  not not_6 (not_6_out, B);
  not not_7 (not_7_out, C);
  and and_9 (and_9_out, _0, not_5_out, not_6_out, not_7_out);
  and and_10 (and_10_out, D, not_5_out, not_6_out, C);
  and and_11 (and_11_out, _0, not_5_out, B, not_7_out);
  and and_12 (and_12_out, not_4_out, not_5_out, B, C);
  and and_13 (and_13_out, D, A, not_6_out, not_7_out);
  and and_14 (and_14_out, _0, A, not_6_out, C);
  and and_15 (and_15_out, not_4_out, A, B, not_7_out);
  and and_16 (and_16_out, D, A, B, C);
  or or_2 (Output, and_9_out, and_10_out, and_11_out, and_12_out, and_13_out, and_14_out, and_15_out, and_16_out);
endmodule
