// Logisim project callButton.circ as structural Verilog: 1 circuit, main circuit main
module main (
  input  Call,
  input  Reset
);

  wire and_1_out, clock_1_out, d_ff_1_q, not_1_out, or_1_out;

  not not_1 (not_1_out, Reset);
  Clock clock_1 (.out(clock_1_out));
  or or_1 (or_1_out, Call, and_1_out);
  and and_1 (and_1_out, not_1_out, d_ff_1_q);
  D_Flip_Flop #(.trigger("falling")) d_ff_1 (
    .clk(clock_1_out), .D(or_1_out), .Q(d_ff_1_q));  // open: Qn, preset, en, reset
  LED led_1 (.in(d_ff_1_q));

  // Notes on the sheet:
  //   Clock
  //   Memory Unit
  //   Signal Light
endmodule
