// Logisim project 7segDisp.circ as structural Verilog: 1 circuit, main circuit main
module main (
  input  in_1,
  input  in_2,
  input  in_3
);

  wire decoder_1_out0, decoder_1_out1, decoder_1_out2, decoder_1_out3, decoder_1_out4, decoder_1_out5,
       decoder_1_out6, decoder_1_out7, or_1_out, or_2_out, or_3_out, or_4_out, or_5_out, or_6_out, or_7_out;

  Decoder #(.select(3), .enable("false")) decoder_1 (
    .out0(decoder_1_out0), .out1(decoder_1_out1), .out2(decoder_1_out2), .out3(decoder_1_out3),
    .out4(decoder_1_out4), .out5(decoder_1_out5), .out6(decoder_1_out6), .out7(decoder_1_out7),
    .sel({in_1, in_2, in_3}));
  or or_1 (or_1_out, decoder_1_out0, decoder_1_out2, decoder_1_out3, decoder_1_out5, decoder_1_out6, decoder_1_out7);
  or or_2 (or_2_out, decoder_1_out0, decoder_1_out1, decoder_1_out3, decoder_1_out4, decoder_1_out5, decoder_1_out6, decoder_1_out7);
  or or_3 (or_3_out, decoder_1_out0, decoder_1_out1, decoder_1_out2, decoder_1_out3, decoder_1_out4, decoder_1_out7);
  or or_4 (or_4_out, decoder_1_out0, decoder_1_out2, decoder_1_out3, decoder_1_out5, decoder_1_out6);
  or or_5 (or_5_out, decoder_1_out0, decoder_1_out4, decoder_1_out5, decoder_1_out6);
  or or_6 (or_6_out, decoder_1_out0, decoder_1_out2, decoder_1_out6);
  or or_7 (or_7_out, decoder_1_out2, decoder_1_out3, decoder_1_out4, decoder_1_out5, decoder_1_out6);
  _7_Segment_Display u_7_segment_display_1 (
    .g(or_7_out), .f(or_5_out), .a(or_1_out), .b(or_3_out), .e(or_6_out), .d(or_4_out), .c(or_2_out));  // open: dp

  // Notes on the sheet:
  //   A
  //   C
  //   B
  //   D
  //   F
  //   E
  //   G
endmodule
