// Logisim project CPE_HW_11.circ as structural Verilog: 1 circuit, main circuit main
module main (
  input  A15,
  input  A14,
  input  A13,
  input  A12,
  input  A11,
  input  A10,
  input  A9,
  input  A8,
  input  A7,
  input  A6,
  input  A5,
  input  A4,
  input  A3,
  input  A2,
  input  A1,
  input  A0
);

  wire and_1_out, and_2_out, and_3_out, and_4_out, nand_1_out, nand_2_out, not_1_out, not_2_out, not_3_out,
       not_4_out, not_5_out, not_6_out, not_7_out, not_8_out, not_9_out, not_10_out, not_11_out, not_12_out,
       not_13_out, not_14_out, not_15_out, not_16_out;

  not not_1 (not_1_out, A14);
  not not_2 (not_2_out, A13);
  and and_1 (and_1_out, A15, A14, not_3_out, not_4_out);
  not not_3 (not_3_out, A13);
  not not_4 (not_4_out, A12);
  not not_5 (not_5_out, A11);
  not not_6 (not_6_out, A10);
  and and_2 (and_2_out, not_5_out, not_6_out, not_7_out, not_8_out);
  not not_7 (not_7_out, A9);
  not not_8 (not_8_out, A8);
  not not_9 (not_9_out, A7);
  not not_10 (not_10_out, A6);
  and and_3 (and_3_out, not_9_out, not_10_out, not_11_out, not_12_out);
  not not_11 (not_11_out, A5);
  not not_12 (not_12_out, A4);
  not not_13 (not_13_out, A3);
  not not_14 (not_14_out, A2);
  and and_4 (and_4_out, not_13_out, not_14_out, not_15_out, not_16_out);
  not not_15 (not_15_out, A1);
  not not_16 (not_16_out, A0);
  nand nand_1 (nand_1_out, A15, not_1_out, not_2_out);
  nand nand_2 (nand_2_out, and_1_out, and_2_out, and_3_out, and_4_out);

  // Notes on the sheet:
  //   TO RAM CS
  //   TO ADC SELECT
endmodule
